// Logisim project 7 Segment Calculator.circ as structural Verilog: 3 circuits, main circuit main
module main (
  input  [3:0] A,
  input  [3:0] B,
  input  MODE,
  input  [3:0] in_4,
  input  [1:0] S,
  output [3:0] out_6
);

  wire adder_1_cout, and_2_out, and_3_out, and_4_out, and_5_out, and_6_out, and_7_out, and_8_out, and_9_out,
       and_10_out, and_11_out, and_12_out, and_13_out, and_14_out, and_15_out, and_16_out, and_17_out,
       and_18_out, and_19_out, and_20_out, and_21_out, and_22_out, and_23_out, and_24_out, and_25_out,
       and_26_out, and_27_out, and_28_out, and_29_out, and_30_out, and_31_out, and_32_out, and_33_out,
       and_34_out, and_35_out, and_36_out, and_37_out, and_38_out, and_39_out, and_40_out, comparator_1_eq,
       comparator_1_gt, comparator_1_lt, not_2_out, not_3_out, not_4_out, not_5_out, not_6_out, not_7_out,
       not_8_out, not_9_out, not_10_out, not_11_out, not_12_out, not_13_out, not_14_out, not_15_out,
       not_16_out, not_17_out, not_18_out, not_19_out, not_20_out, not_21_out, not_22_out, not_23_out,
       not_24_out, not_25_out, not_26_out, not_27_out, not_28_out, not_29_out, not_30_out, not_31_out,
       not_32_out, not_33_out, not_34_out, not_35_out, not_36_out, not_37_out, not_38_out, not_39_out,
       not_40_out, not_41_out, not_42_out, not_43_out, not_44_out, not_45_out, not_46_out, not_47_out,
       not_48_out, not_49_out, not_50_out, not_51_out, not_52_out, not_53_out, not_54_out, not_55_out,
       not_56_out, not_57_out, not_58_out, not_59_out, not_60_out, not_61_out, not_62_out, not_63_out,
       not_64_out, not_65_out, not_66_out, not_67_out, not_68_out, not_69_out, not_70_out, not_71_out,
       not_72_out, not_73_out, not_74_out, not_75_out, not_76_out, not_77_out, not_78_out, not_79_out,
       not_80_out, not_81_out, or_2_out, or_3_out, or_4_out, or_5_out, or_6_out, or_7_out, or_8_out,
       subtractor_1_bout;
  wire [3:0] adder_1_out, adder_2_out, and_1_out, multiplexer_1_out, multiplexer_2_out, negator_1_out,
       not_1_out, or_1_out, subtractor_1_out, xor_1_out;

  Comparator #(.width(4), .mode("unsigned")) comparator_1 (
    .a(A), .b(B), .gt(comparator_1_gt), .eq(comparator_1_eq), .lt(comparator_1_lt));
  LED_part u_A (.in(comparator_1_gt));
  LED_part led (.in(comparator_1_eq));
  LED_part u_B (.in(comparator_1_lt));
  Adder #(.width(4)) adder_1 (.a(A), .b(B), .out(adder_1_out), .cout(adder_1_cout));  // open: cin
  LED_part _1 (.in(adder_1_cout));
  Subtractor #(.width(4)) subtractor_1 (.a(A), .b(B), .out(subtractor_1_out), .bout(subtractor_1_bout));  // open: bin
  LED_part _1_2 (.in(subtractor_1_bout));
  Negator #(.width(4)) negator_1 (.in(B), .out(negator_1_out));
  Adder #(.width(4)) adder_2 (.a(A), .b(in_4), .out(adder_2_out));  // open: cin, cout
  assign and_1_out = A & B;  // AND_Gate and_1, 4 bits wide
  assign or_1_out = A | B;  // OR_Gate or_1, 4 bits wide
  assign xor_1_out = A ^ B;  // XOR_Gate xor_1, 4 bits wide
  assign not_1_out = ~A;  // NOT_Gate not_1, 4 bits wide
  Multiplexer #(.select(2), .width(4)) multiplexer_1 (
    .in0(adder_1_out), .in1(subtractor_1_out), .in2(negator_1_out), .in3(adder_2_out),
    .out(multiplexer_1_out), .sel(S));  // open: en
  Multiplexer #(.select(2), .width(4)) multiplexer_2 (
    .in0(and_1_out), .in1(or_1_out), .in2(xor_1_out), .in3(not_1_out), .out(multiplexer_2_out), .sel(S));  // open: en
  Multiplexer #(.width(4)) multiplexer_3 (
    .in0(multiplexer_1_out), .in1(multiplexer_2_out), .out(out_6), .sel(MODE));  // open: en
  and and_2 (and_2_out, MODE, out_6[3]);
  LED_part led_2 (.in(and_2_out));
  LED_part led_3 (.in(and_3_out));
  and and_3 (and_3_out, MODE, out_6[2]);
  and and_4 (and_4_out, MODE, out_6[1]);
  LED_part led_4 (.in(and_4_out));
  and and_5 (and_5_out, MODE, out_6[0]);
  LED_part led_5 (.in(and_5_out));
  not not_2 (not_2_out, MODE);
  not not_3 (not_3_out, out_6[2]);
  not not_4 (not_4_out, out_6[0]);
  not not_5 (not_5_out, MODE);
  not not_6 (not_6_out, out_6[3]);
  not not_7 (not_7_out, MODE);
  not not_8 (not_8_out, out_6[3]);
  not not_9 (not_9_out, MODE);
  not not_10 (not_10_out, MODE);
  not not_11 (not_11_out, out_6[2]);
  not not_12 (not_12_out, out_6[1]);
  not not_13 (not_13_out, MODE);
  not not_14 (not_14_out, out_6[0]);
  not not_15 (not_15_out, MODE);
  not not_16 (not_16_out, out_6[3]);
  not not_17 (not_17_out, out_6[1]);
  not not_18 (not_18_out, out_6[0]);
  not not_19 (not_19_out, MODE);
  not not_20 (not_20_out, out_6[2]);
  not not_21 (not_21_out, out_6[1]);
  not not_22 (not_22_out, MODE);
  not not_23 (not_23_out, out_6[2]);
  not not_24 (not_24_out, out_6[0]);
  not not_25 (not_25_out, MODE);
  not not_26 (not_26_out, out_6[3]);
  not not_27 (not_27_out, MODE);
  not not_28 (not_28_out, out_6[1]);
  not not_29 (not_29_out, MODE);
  not not_30 (not_30_out, out_6[2]);
  not not_31 (not_31_out, out_6[1]);
  not not_32 (not_32_out, MODE);
  not not_33 (not_33_out, out_6[3]);
  not not_34 (not_34_out, MODE);
  not not_35 (not_35_out, out_6[1]);
  not not_36 (not_36_out, MODE);
  not not_37 (not_37_out, out_6[3]);
  not not_38 (not_38_out, MODE);
  not not_39 (not_39_out, out_6[2]);
  not not_40 (not_40_out, MODE);
  not not_41 (not_41_out, out_6[3]);
  not not_42 (not_42_out, out_6[2]);
  not not_43 (not_43_out, out_6[0]);
  not not_44 (not_44_out, MODE);
  not not_45 (not_45_out, out_6[2]);
  not not_46 (not_46_out, MODE);
  not not_47 (not_47_out, out_6[1]);
  not not_48 (not_48_out, MODE);
  not not_49 (not_49_out, out_6[0]);
  not not_50 (not_50_out, MODE);
  not not_51 (not_51_out, out_6[1]);
  not not_52 (not_52_out, MODE);
  not not_53 (not_53_out, out_6[2]);
  not not_54 (not_54_out, out_6[0]);
  not not_55 (not_55_out, MODE);
  not not_56 (not_56_out, out_6[0]);
  not not_57 (not_57_out, MODE);
  not not_58 (not_58_out, MODE);
  not not_59 (not_59_out, MODE);
  not not_60 (not_60_out, out_6[1]);
  not not_61 (not_61_out, out_6[0]);
  not not_62 (not_62_out, MODE);
  not not_63 (not_63_out, out_6[3]);
  not not_64 (not_64_out, out_6[1]);
  not not_65 (not_65_out, MODE);
  not not_66 (not_66_out, out_6[0]);
  not not_67 (not_67_out, MODE);
  not not_68 (not_68_out, out_6[2]);
  not not_69 (not_69_out, MODE);
  not not_70 (not_70_out, MODE);
  not not_71 (not_71_out, out_6[3]);
  not not_72 (not_72_out, out_6[2]);
  not not_73 (not_73_out, MODE);
  not not_74 (not_74_out, out_6[3]);
  not not_75 (not_75_out, out_6[1]);
  not not_76 (not_76_out, MODE);
  not not_77 (not_77_out, out_6[0]);
  not not_78 (not_78_out, MODE);
  not not_79 (not_79_out, out_6[2]);
  not not_80 (not_80_out, out_6[1]);
  not not_81 (not_81_out, MODE);
  and and_6 (and_6_out, not_2_out, not_3_out, not_4_out);
  and and_7 (and_7_out, not_5_out, not_6_out, out_6[1]);
  and and_8 (and_8_out, not_7_out, not_8_out, out_6[2], out_6[0]);
  and and_9 (and_9_out, not_9_out, out_6[2], out_6[1]);
  and and_10 (and_10_out, not_10_out, out_6[3], not_11_out, not_12_out);
  and and_11 (and_11_out, not_13_out, out_6[3], not_14_out);
  and and_12 (and_12_out, not_15_out, not_16_out, not_17_out, not_18_out);
  and and_13 (and_13_out, not_19_out, not_20_out, not_21_out);
  and and_14 (and_14_out, not_22_out, not_23_out, not_24_out);
  and and_15 (and_15_out, not_25_out, not_26_out, out_6[1], out_6[0]);
  and and_16 (and_16_out, not_27_out, out_6[3], not_28_out, out_6[0]);
  and and_17 (and_17_out, not_29_out, not_30_out, not_31_out);
  and and_18 (and_18_out, not_32_out, not_33_out, out_6[0]);
  and and_19 (and_19_out, not_34_out, not_35_out, out_6[0]);
  and and_20 (and_20_out, not_36_out, not_37_out, out_6[2]);
  and and_21 (and_21_out, not_38_out, out_6[3], not_39_out);
  and and_22 (and_22_out, not_40_out, not_41_out, not_42_out, not_43_out);
  and and_23 (and_23_out, not_44_out, not_45_out, out_6[1], out_6[0]);
  and and_24 (and_24_out, not_46_out, out_6[2], not_47_out, out_6[0]);
  and and_25 (and_25_out, not_48_out, out_6[2], out_6[1], not_49_out);
  and and_26 (and_26_out, not_50_out, out_6[3], not_51_out);
  and and_27 (and_27_out, not_52_out, not_53_out, not_54_out);
  and and_28 (and_28_out, not_55_out, out_6[1], not_56_out);
  and and_29 (and_29_out, not_57_out, out_6[3], out_6[1]);
  and and_30 (and_30_out, not_58_out, out_6[3], out_6[2]);
  and and_31 (and_31_out, not_59_out, not_60_out, not_61_out);
  and and_32 (and_32_out, not_62_out, not_63_out, out_6[2], not_64_out);
  and and_33 (and_33_out, not_65_out, out_6[2], not_66_out);
  and and_34 (and_34_out, not_67_out, out_6[3], not_68_out);
  and and_35 (and_35_out, not_69_out, out_6[3], out_6[1]);
  and and_36 (and_36_out, not_70_out, not_71_out, not_72_out, out_6[1]);
  and and_37 (and_37_out, not_73_out, not_74_out, out_6[2], not_75_out);
  and and_38 (and_38_out, not_76_out, out_6[2], out_6[1], not_77_out);
  and and_39 (and_39_out, not_78_out, out_6[3], not_79_out, not_80_out);
  and and_40 (and_40_out, not_81_out, out_6[3], out_6[0]);
  or or_2 (or_2_out, and_6_out, and_7_out, and_8_out, and_9_out, and_10_out, and_11_out);
  or or_3 (or_3_out, and_12_out, and_13_out, and_14_out, and_15_out, and_16_out);
  or or_4 (or_4_out, and_17_out, and_18_out, and_19_out, and_20_out, and_21_out);
  or or_5 (or_5_out, and_22_out, and_23_out, and_24_out, and_25_out, and_26_out);
  or or_6 (or_6_out, and_27_out, and_28_out, and_29_out, and_30_out);
  or or_7 (or_7_out, and_31_out, and_32_out, and_33_out, and_34_out, and_35_out);
  or or_8 (or_8_out, and_36_out, and_37_out, and_38_out, and_39_out, and_40_out);
  _7_Segment_Display u_7_segment_display_1 (
    .g(or_8_out), .f(or_7_out), .a(or_2_out), .b(or_3_out), .e(or_6_out), .d(or_5_out), .c(or_4_out));  // open: dp

  // Notes on the sheet:
  //   C0
  //   CS
endmodule

module _7_SEG (
  input  M,
  input  W,
  input  X,
  input  Y,
  input  Z
);

  wire and_1_out, and_2_out, and_3_out, and_4_out, and_5_out, and_6_out, and_7_out, and_8_out, and_9_out,
       and_10_out, and_11_out, and_12_out, and_13_out, and_14_out, and_15_out, and_16_out, and_17_out,
       and_18_out, and_19_out, and_20_out, and_21_out, and_22_out, and_23_out, and_24_out, and_25_out,
       and_26_out, and_27_out, and_28_out, and_29_out, and_30_out, and_31_out, and_32_out, and_33_out,
       and_34_out, and_35_out, not_1_out, not_2_out, not_3_out, not_4_out, not_5_out, not_6_out, not_7_out,
       not_8_out, not_9_out, not_10_out, not_11_out, not_12_out, not_13_out, not_14_out, not_15_out,
       not_16_out, not_17_out, not_18_out, not_19_out, not_20_out, not_21_out, not_22_out, not_23_out,
       not_24_out, not_25_out, not_26_out, not_27_out, not_28_out, not_29_out, not_30_out, not_31_out,
       not_32_out, not_33_out, not_34_out, not_35_out, not_36_out, not_37_out, not_38_out, not_39_out,
       not_40_out, not_41_out, not_42_out, not_43_out, not_44_out, not_45_out, not_46_out, not_47_out,
       not_48_out, not_49_out, not_50_out, not_51_out, not_52_out, not_53_out, not_54_out, not_55_out,
       not_56_out, not_57_out, not_58_out, not_59_out, not_60_out, not_61_out, not_62_out, not_63_out,
       not_64_out, not_65_out, not_66_out, not_67_out, not_68_out, not_69_out, not_70_out, not_71_out,
       not_72_out, not_73_out, not_74_out, not_75_out, not_76_out, not_77_out, not_78_out, not_79_out,
       not_80_out, or_1_out, or_2_out, or_3_out, or_4_out, or_5_out, or_6_out, or_7_out;

  not not_1 (not_1_out, M);
  not not_2 (not_2_out, X);
  not not_3 (not_3_out, Z);
  not not_4 (not_4_out, M);
  not not_5 (not_5_out, W);
  not not_6 (not_6_out, M);
  not not_7 (not_7_out, W);
  not not_8 (not_8_out, M);
  not not_9 (not_9_out, M);
  not not_10 (not_10_out, X);
  not not_11 (not_11_out, Y);
  not not_12 (not_12_out, M);
  not not_13 (not_13_out, Z);
  not not_14 (not_14_out, M);
  not not_15 (not_15_out, W);
  not not_16 (not_16_out, Y);
  not not_17 (not_17_out, Z);
  not not_18 (not_18_out, M);
  not not_19 (not_19_out, X);
  not not_20 (not_20_out, Y);
  not not_21 (not_21_out, M);
  not not_22 (not_22_out, X);
  not not_23 (not_23_out, Z);
  not not_24 (not_24_out, M);
  not not_25 (not_25_out, W);
  not not_26 (not_26_out, M);
  not not_27 (not_27_out, Y);
  not not_28 (not_28_out, M);
  not not_29 (not_29_out, X);
  not not_30 (not_30_out, Y);
  not not_31 (not_31_out, M);
  not not_32 (not_32_out, W);
  not not_33 (not_33_out, M);
  not not_34 (not_34_out, Y);
  not not_35 (not_35_out, M);
  not not_36 (not_36_out, W);
  not not_37 (not_37_out, M);
  not not_38 (not_38_out, X);
  not not_39 (not_39_out, M);
  not not_40 (not_40_out, W);
  not not_41 (not_41_out, X);
  not not_42 (not_42_out, Z);
  not not_43 (not_43_out, M);
  not not_44 (not_44_out, X);
  not not_45 (not_45_out, M);
  not not_46 (not_46_out, Y);
  not not_47 (not_47_out, M);
  not not_48 (not_48_out, Z);
  not not_49 (not_49_out, M);
  not not_50 (not_50_out, Y);
  not not_51 (not_51_out, M);
  not not_52 (not_52_out, X);
  not not_53 (not_53_out, Z);
  not not_54 (not_54_out, M);
  not not_55 (not_55_out, Z);
  not not_56 (not_56_out, M);
  not not_57 (not_57_out, M);
  not not_58 (not_58_out, M);
  not not_59 (not_59_out, Y);
  not not_60 (not_60_out, Z);
  not not_61 (not_61_out, M);
  not not_62 (not_62_out, W);
  not not_63 (not_63_out, Y);
  not not_64 (not_64_out, M);
  not not_65 (not_65_out, Z);
  not not_66 (not_66_out, M);
  not not_67 (not_67_out, X);
  not not_68 (not_68_out, M);
  not not_69 (not_69_out, M);
  not not_70 (not_70_out, W);
  not not_71 (not_71_out, X);
  not not_72 (not_72_out, M);
  not not_73 (not_73_out, W);
  not not_74 (not_74_out, Y);
  not not_75 (not_75_out, M);
  not not_76 (not_76_out, Z);
  not not_77 (not_77_out, M);
  not not_78 (not_78_out, X);
  not not_79 (not_79_out, Y);
  not not_80 (not_80_out, M);
  and and_1 (and_1_out, not_1_out, not_2_out, not_3_out);
  and and_2 (and_2_out, not_4_out, not_5_out, Y);
  and and_3 (and_3_out, not_6_out, not_7_out, X, Z);
  and and_4 (and_4_out, not_8_out, X, Y);
  and and_5 (and_5_out, not_9_out, W, not_10_out, not_11_out);
  and and_6 (and_6_out, not_12_out, W, not_13_out);
  and and_7 (and_7_out, not_14_out, not_15_out, not_16_out, not_17_out);
  and and_8 (and_8_out, not_18_out, not_19_out, not_20_out);
  and and_9 (and_9_out, not_21_out, not_22_out, not_23_out);
  and and_10 (and_10_out, not_24_out, not_25_out, Y, Z);
  and and_11 (and_11_out, not_26_out, W, not_27_out, Z);
  and and_12 (and_12_out, not_28_out, not_29_out, not_30_out);
  and and_13 (and_13_out, not_31_out, not_32_out, Z);
  and and_14 (and_14_out, not_33_out, not_34_out, Z);
  and and_15 (and_15_out, not_35_out, not_36_out, X);
  and and_16 (and_16_out, not_37_out, W, not_38_out);
  and and_17 (and_17_out, not_39_out, not_40_out, not_41_out, not_42_out);
  and and_18 (and_18_out, not_43_out, not_44_out, Y, Z);
  and and_19 (and_19_out, not_45_out, X, not_46_out, Z);
  and and_20 (and_20_out, not_47_out, X, Y, not_48_out);
  and and_21 (and_21_out, not_49_out, W, not_50_out);
  and and_22 (and_22_out, not_51_out, not_52_out, not_53_out);
  and and_23 (and_23_out, not_54_out, Y, not_55_out);
  and and_24 (and_24_out, not_56_out, W, Y);
  and and_25 (and_25_out, not_57_out, W, X);
  and and_26 (and_26_out, not_58_out, not_59_out, not_60_out);
  and and_27 (and_27_out, not_61_out, not_62_out, X, not_63_out);
  and and_28 (and_28_out, not_64_out, X, not_65_out);
  and and_29 (and_29_out, not_66_out, W, not_67_out);
  and and_30 (and_30_out, not_68_out, W, Y);
  and and_31 (and_31_out, not_69_out, not_70_out, not_71_out, Y);
  and and_32 (and_32_out, not_72_out, not_73_out, X, not_74_out);
  and and_33 (and_33_out, not_75_out, X, Y, not_76_out);
  and and_34 (and_34_out, not_77_out, W, not_78_out, not_79_out);
  and and_35 (and_35_out, not_80_out, W, Z);
  or or_1 (or_1_out, and_1_out, and_2_out, and_3_out, and_4_out, and_5_out, and_6_out);
  or or_2 (or_2_out, and_7_out, and_8_out, and_9_out, and_10_out, and_11_out);
  or or_3 (or_3_out, and_12_out, and_13_out, and_14_out, and_15_out, and_16_out);
  or or_4 (or_4_out, and_17_out, and_18_out, and_19_out, and_20_out, and_21_out);
  or or_5 (or_5_out, and_22_out, and_23_out, and_24_out, and_25_out);
  or or_6 (or_6_out, and_26_out, and_27_out, and_28_out, and_29_out, and_30_out);
  or or_7 (or_7_out, and_31_out, and_32_out, and_33_out, and_34_out, and_35_out);
  _7_Segment_Display u_7_segment_display_1 (
    .g(or_7_out), .f(or_6_out), .a(or_1_out), .b(or_2_out), .e(or_5_out), .d(or_4_out), .c(or_3_out));  // open: dp
endmodule

module LED (
  input  M,
  input  W,
  input  X,
  input  Y,
  input  Z,
  output W_2,
  output X_2,
  output Y_2,
  output Z_2
);

  and and_1 (W_2, M, W);
  and and_2 (X_2, M, X);
  and and_3 (Y_2, M, Y);
  and and_4 (Z_2, M, Z);
endmodule
